# Fritzing sketch PumpTest (saved by Fritzing 1.0.1rc)
breadboards: 1

parts:
  A1 = Particle - Photon2
  Relay1 = Relay - 6 pins [package="DIP (Dual Inline) [THT]"]
  Q1 = PNP-Transistor [package="TO92 [THT]"]
  M1 = DC Motor [voltage_(max)=6V voltage_(min)=3V]
  R1 = Resistor [tolerance=±5% resistance=220 package="2512 [SMD]"]
  R2 = Resistor [tolerance=±5% resistance=2.2k package="2512 [SMD]"]
  J1 = Camdenboss CTB0158-2 [part_number=CTB0158-2 package=THT]

nets:
  3.3V: A1.Pin_2, Relay1.VCC
  GND: A1.Pin_4, Relay1.GND, Q1.E, R2.Pin_0
  N1: A1.Pin_9, Q1.B, R2.Pin_1
  5V: A1.Pin_26, R1.Pin_1
  N2: Relay1.IN, Q1.C, R1.Pin_0
  N3: Relay1.COM, M1.pin_1
  N4: Relay1.ON, J1.pin1
  N5: M1.pin_2, J1.pin2

notes:
  External 5V Power Supply

custom parts:
  Particle - Photon2: The Photon 2 is a microcontroller and Wi-Fi networking developed by particle. Features: 802.11a/b/g/n Wi-Fi, 2.4 GHz and 5 GHz Integrated PCB antenna Integrated U.FL connector for external antenna Integrated RF switch BLE 5 using same antenna as Wi-Fi Realtek RTL8721DM MCU ARM Cortex M33 CPU, 200 MHz 2048 KB (2 MB) user application maximum size 3072 KB (3 MB) of RAM available to user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
  Relay - 6 pins: A DIP stand-in part for whatever IC you want. With 6 pins on a 900mil dual inline package (DIP) footprint.
